# Fritzing sketch RobotHeadToy (saved by Fritzing 0.3.6b)
breadboards: 1

parts:
  Arduino1 = Arduino
  LED1 = Red LED - 5mm
  R1 = Rotary Potentiometer (Large) [package=THT]
  R2 = Rotary Potentiometer (Large) [package=THT]
  LED1_2 = Red LED - 5mm
  LED1_3 = Red LED - 5mm
  LED1_4 = Red LED - 5mm
  U1 = Mystery Part - 3 pins [package=THT]
  U1_2 = Mystery Part - 3 pins [package=THT]
  U1_3 = Mystery Part - 3 pins [package=THT]
  S1 = Pushbutton [package=THT]
  S1_2 = Pushbutton [package=THT]
  R3 = 220 Ω Resistor [package=THT]
  R3_2 = 220 Ω Resistor [package=THT]
  R3_3 = 220 Ω Resistor [package=THT]
  R3_4 = 220 Ω Resistor [package=THT]
  R3_5 = 220 Ω Resistor [package=THT]
  R3_6 = 220 Ω Resistor [package=THT]
  J1 = Piezo Speaker
  LED1_5 = Red LED - 5mm
  LED1_6 = Red LED - 5mm
  R3_7 = 220 Ω Resistor [package=THT]
  R3_8 = 220 Ω Resistor [package=THT]
  R3_9 = 220 Ω Resistor [package=THT]
  R3_10 = 220 Ω Resistor [package=THT]
  U2 = Mystery Part - 3 pins [package=THT]

nets:
  N1: Arduino1.D13, S1.leg0
  N2: Arduino1.D12, Arduino1.D6, S1_2.leg0, R3.Pin_1
  N3: Arduino1.D11, R3_10.Pin_1
  N4: Arduino1.D10, R3_9.Pin_1
  N5: Arduino1.D9, Arduino1.D7, Arduino1.D4, Arduino1.D2, R3_2.Pin_1, R3_4.Pin_1, R3_6.Pin_1, R3_8.Pin_1
  N6: Arduino1.D8, Arduino1.D5, Arduino1.D3, R3_3.Pin_1, R3_5.Pin_1, R3_7.Pin_1
  N7: Arduino1.+5V, R1.leg2, R2.leg2, U1_2.leg1, U1_3.leg1
  N8: Arduino1.GND, R1.leg1, R2.leg1, U1.leg3, U1_2.leg3, U1_3.leg3, S1.leg1, S1_2.leg1, J1.pin1
  N9: Arduino1.A0, R1.wiper
  N10: Arduino1.A1, U1.leg2
  N11: Arduino1.A2, U1_2.leg2
  N12: Arduino1.A3, U1_3.leg2
  N13: Arduino1.A4, R2.wiper
  N14: LED1.cathode, LED1_2.cathode, LED1_3.cathode, LED1_4.cathode, LED1_5.cathode, LED1_6.cathode
  N15: LED1.anode, R3_2.Pin_0
  N16: LED1_2.anode, R3_3.Pin_0
  N17: LED1_3.anode, R3_4.Pin_0
  N18: LED1_4.anode, R3_5.Pin_0
  N19: R3.Pin_0, J1.pin2
  N20: R3_6.Pin_0, R3_9.Pin_0, R3_10.Pin_0, U2.leg1, U2.leg2, U2.leg3
  N21: LED1_5.anode, R3_7.Pin_0
  N22: LED1_6.anode, R3_8.Pin_0
